// Logisim project s-mips.circ as structural Verilog: 10 circuits, main circuit S-MIPS Board
module S_MIPS_Board (
  input  DESHABILITAR_DISPATCHER,
  output halt
);

  wire button_1_out, CLK, CS, d_ff_1_q, LCLR, LoadRAM, LoadRAMOn, LW, R_R_W, R_W, ram_dispatcher_1_finished,
       RCS, Reset_out, RST, TTY_EN;
  wire [2:0] KDB;
  wire [3:0] LMask, Mask, ram_1_read_time, ram_1_write_time, RMask;
  wire [6:0] KDB_DATA, TTY_DATA;
  wire [15:0] Addr, LAddr, RAddr;
  wire [31:0] I0, I1, I2, I3, LData, ram_1_data_out_0, ram_1_data_out_1, ram_1_data_out_2, ram_1_data_out_3,
       RI0, RI1, RI2, RI3;

  TTY #(.rows(25), .cols(80)) tty_1 (.data(TTY_DATA), .clk(CLK), .we(TTY_EN), .clr(RST));
  not not_1 (LoadRAMOn, ram_dispatcher_1_finished);
  RAM_Dispatcher ram_dispatcher_1 (
    .WriteTime(ram_1_write_time), .Clock(CLK), .Data(LData), .Address(LAddr), .Mask(LMask),
    .Finished(ram_dispatcher_1_finished), .Write(LW), .CLR(LCLR));
  Keyboard #(.buflen(64)) keyboard_1 (.clk(CLK), .re(KDB[0]), .avail(KDB[2]), .data(KDB_DATA));  // open: clr
  RAM ram_1 (
    .Address(RAddr), .Data_Out_0(ram_1_data_out_0), .Data_Out_1(ram_1_data_out_1),
    .Data_Out_2(ram_1_data_out_2), .Data_Out_3(ram_1_data_out_3), .Data_In_0(RI0), .Data_In_1(RI1),
    .Data_In_2(RI2), .Data_In_3(RI3), .Mask(RMask), .nRead_Write(R_R_W), .Chip_Select(RCS),
    .Read_Time(ram_1_read_time), .Reset(button_1_out), .Write_Time(ram_1_write_time));
  Button button_1 (.out(button_1_out));
  D_Flip_Flop d_ff_1 (.clk(CLK), .D(1'b1), .Q(d_ff_1_q), .reset(Reset_out));  // open: Qn, preset, en
  Button Reset (.out(Reset_out));
  S_MIPS s_mips_1 (
    .Kbd_Enable(KDB[0]), .Address(Addr), .Kbd_Clear(KDB[1]), .Kbd_Available(KDB[2]), .RAM_In_0(I0),
    .Kbd_ASCII_Data(KDB_DATA), .RAM_In_1(I1), .TTY_Enable(TTY_EN), .RAM_In_2(I2), .RAM_In_3(I2),
    .TTY_ASCII_Data(TTY_DATA), .Reset(RST), .RAM_Out_0(ram_1_data_out_0), .Clock(CLK),
    .RAM_Out_1(ram_1_data_out_1), .Stop(halt), .RAM_Out_2(ram_1_data_out_2), .RAM_Out_3(ram_1_data_out_3),
    .Mask(Mask), .Read_Time(ram_1_read_time), .Write_Time(ram_1_write_time), .nRead_Write(R_W),
    .Chip_Select(CS));
  D_Flip_Flop d_ff_2 (.clk(CLK), .D(d_ff_1_q), .Qn(LCLR), .reset(Reset_out));  // open: Q, preset, en
  or or_1 (RST, LCLR, LoadRAM);
  Clock clock_1 (.out(CLK));
  Multiplexer #(.width(32), .enable("false")) multiplexer_1 (.in0(I0), .in1(LData), .out(RI0), .sel(LoadRAM));
  Multiplexer #(.width(32), .enable("false")) multiplexer_2 (.in0(I1), .in1(LData), .out(RI1), .sel(LoadRAM));
  Multiplexer #(.width(32), .enable("false")) multiplexer_3 (.in0(I2), .in1(LData), .out(RI2), .sel(LoadRAM));
  Multiplexer #(.width(32), .enable("false")) multiplexer_4 (.in0(I3), .in1(LData), .out(RI3), .sel(LoadRAM));
  and and_1 (LoadRAM, ~DESHABILITAR_DISPATCHER, LoadRAMOn);  // AND_Gate
  Multiplexer #(.width(16), .enable("false")) multiplexer_5 (.in0(Addr), .in1(LAddr), .out(RAddr), .sel(LoadRAM));
  Multiplexer #(.width(4), .enable("false")) multiplexer_6 (.in0(Mask), .in1(LMask), .out(RMask), .sel(LoadRAM));
  Multiplexer #(.enable("false")) multiplexer_7 (.in0(CS), .in1(LW), .out(RCS), .sel(LoadRAM));
  Multiplexer #(.enable("false")) multiplexer_8 (.in0(R_W), .in1(LW), .out(R_R_W), .sel(LoadRAM));

  // Notes on the sheet:
  //   NO MODIFICAR
  //   Keyboard
endmodule

module RAM (
  input  [15:0] Address,
  input  [31:0] Data_In_0,
  input  [31:0] Data_In_1,
  input  [31:0] Data_In_2,
  input  [31:0] Data_In_3,
  input  [3:0] Mask,
  input  nRead_Write,
  input  Chip_Select,
  input  Reset,
  output [31:0] Data_Out_0,
  output [31:0] Data_Out_1,
  output [31:0] Data_Out_2,
  output [31:0] Data_Out_3,
  output [3:0] Read_Time,
  output [3:0] Write_Time
);

  wire and_2_out, and_3_out, and_4_out, and_5_out, and_6_out, and_7_out, and_8_out, and_9_out, Changed, CLK,
       comparator_2_eq, comparator_3_eq, comparator_4_eq, comparator_5_eq, comparator_6_eq, Count,
       demultiplexer_3_out0, Idle, Idle_q, Load, Load0, Load1, nand_1_out, or_1_out, or_2_out, or_3_out,
       or_4_out, or_5_out, or_6_out, or_7_out, or_8_out, or_9_out, or_10_out, Proc_q, Update_Mem, Zero_Time;
  wire [3:0] counter_1_q, multiplexer_1_out, subtractor_1_out;
  wire [31:0] register_1_q, register_2_q, register_3_q, register_4_q, register_5_q;

  // Probe on 4'b0011
  // Probe on 4'b0010
  Multiplexer #(.width(4), .enable("false")) multiplexer_1 (
    .in0(4'b0011), .in1(4'b0010), .out(multiplexer_1_out), .sel(nRead_Write));
  or or_1 (or_1_out, Idle, Update_Mem);
  or or_2 (or_2_out, ~Chip_Select, Reset);  // OR_Gate
  Subtractor #(.width(4)) subtractor_1 (.a(multiplexer_1_out), .b(4'b0010), .out(subtractor_1_out));  // open: bin, bout
  D_Flip_Flop u_Idle (.clk(CLK), .D(or_1_out), .Q(Idle_q), .preset(or_2_out));  // open: Qn, en, reset
  Demultiplexer #(.enable("false")) demultiplexer_1 (.out0(Idle), .out1(Load0), .in(Idle_q), .sel(Changed));
  // Probe on counter_1_q
  Counter #(.width(4), .max('hf)) counter_1 (
    .load(Load), .D(subtractor_1_out), .count(Count), .Q(counter_1_q), .clk(CLK), .clr(or_3_out));  // open: carry
  or or_3 (or_3_out, ~Chip_Select, Reset);  // OR_Gate
  Comparator #(.width(4), .mode("unsigned")) comparator_1 (
    .a(4'b0000), .b(counter_1_q), .eq(Zero_Time));  // open: gt, lt
  or or_4 (or_4_out, Count, Load0, Load1);
  Register #(.width(32)) register_1 (.D(Data_In_0), .en(Chip_Select), .Q(register_1_q), .clk(CLK), .clr(or_5_out));
  or or_5 (or_5_out, ~Chip_Select, Reset);  // OR_Gate
  Register #(.width(32)) register_2 (.D(Data_In_1), .en(Chip_Select), .Q(register_2_q), .clk(CLK), .clr(or_6_out));
  or or_6 (or_6_out, ~Chip_Select, Reset);  // OR_Gate
  Register #(.width(32)) register_3 (.D(Data_In_2), .en(Chip_Select), .Q(register_3_q), .clk(CLK), .clr(or_7_out));
  or or_7 (or_7_out, ~Chip_Select, Reset);  // OR_Gate
  Register #(.width(32)) register_4 (.D(Data_In_3), .en(Chip_Select), .Q(register_4_q), .clk(CLK), .clr(or_8_out));
  or or_8 (or_8_out, ~Chip_Select, Reset);  // OR_Gate
  Register #(.width(32)) register_5 (
    .D({{11{1'b1}}, nRead_Write, Mask, Address}), .en(Chip_Select), .Q(register_5_q), .clk(CLK),
    .clr(or_9_out));
  or or_9 (or_9_out, ~Chip_Select, Reset);  // OR_Gate
  D_Flip_Flop Proc (.clk(CLK), .D(or_4_out), .Q(Proc_q), .reset(or_10_out));  // open: Qn, preset, en
  or or_10 (or_10_out, ~Chip_Select, Reset);  // OR_Gate
  Demultiplexer #(.enable("false")) demultiplexer_2 (
    .out0(Count), .out1(Update_Mem), .in(demultiplexer_3_out0), .sel(Zero_Time));
  Demultiplexer #(.enable("false")) demultiplexer_3 (
    .out0(demultiplexer_3_out0), .out1(Load1), .in(Proc_q), .sel(Changed));
  Clock clock_1 (.out(CLK));
  Comparator #(.width(32)) comparator_2 (.a(register_1_q), .b(Data_In_0), .eq(comparator_2_eq));  // open: gt, lt
  Comparator #(.width(32)) comparator_3 (.a(register_2_q), .b(Data_In_1), .eq(comparator_3_eq));  // open: gt, lt
  Comparator #(.width(32)) comparator_4 (.a(register_3_q), .b(Data_In_2), .eq(comparator_4_eq));  // open: gt, lt
  Comparator #(.width(32)) comparator_5 (.a(register_4_q), .b(Data_In_3), .eq(comparator_5_eq));  // open: gt, lt
  Comparator #(.width(32)) comparator_6 (
    .a(register_5_q), .b({{11{1'b1}}, nRead_Write, Mask, Address}), .eq(comparator_6_eq));  // open: gt, lt
  nand nand_1 (nand_1_out, comparator_6_eq, comparator_2_eq, comparator_3_eq, comparator_4_eq, comparator_5_eq);
  and and_1 (Changed, nand_1_out, Chip_Select);
  or or_11 (Load, Count, Load1, Load0);
  and and_2 (and_2_out, Mask[0], Update_Mem, nRead_Write);
  and and_3 (and_3_out, Mask[1], Update_Mem, nRead_Write);
  and and_4 (and_4_out, Mask[2], Update_Mem, nRead_Write);
  and and_5 (and_5_out, Mask[3], Update_Mem, nRead_Write);
  RAM_part #(.addrWidth(16), .dataWidth(32), .bus("separate")) ram_1 (
    .addr(Address), .din(Data_In_0), .data(Data_Out_0), .str(and_2_out), .sel(Chip_Select), .clk(CLK),
    .ld(and_6_out), .clr(Reset));
  and and_6 (and_6_out, ~nRead_Write, Idle);  // AND_Gate
  RAM_part #(.addrWidth(16), .dataWidth(32), .bus("separate")) ram_2 (
    .addr(Address), .din(Data_In_1), .data(Data_Out_1), .str(and_3_out), .sel(Chip_Select), .clk(CLK),
    .ld(and_7_out), .clr(Reset));
  and and_7 (and_7_out, ~nRead_Write, Idle);  // AND_Gate
  RAM_part #(.addrWidth(16), .dataWidth(32), .bus("separate")) ram_3 (
    .addr(Address), .din(Data_In_2), .data(Data_Out_2), .str(and_4_out), .sel(Chip_Select), .clk(CLK),
    .ld(and_8_out), .clr(Reset));
  and and_8 (and_8_out, ~nRead_Write, Idle);  // AND_Gate
  RAM_part #(.addrWidth(16), .dataWidth(32), .bus("separate")) ram_4 (
    .addr(Address), .din(Data_In_3), .data(Data_Out_3), .str(and_5_out), .sel(Chip_Select), .clk(CLK),
    .ld(and_9_out), .clr(Reset));
  and and_9 (and_9_out, ~nRead_Write, Idle);  // AND_Gate

  assign Read_Time = 4'b0011;
  assign Write_Time = 4'b0010;

  // Other names for the same wires on the sheet: M0 = Mask[0]; M1 = Mask[1]; M2 = Mask[2]; M3 = Mask[3];
  //   RW = nRead_Write; CLR = Reset; CS = Chip_Select; Load2 = Count

  // Notes on the sheet:
  //   NO MODIFICAR
  //   excepto quizás los valores RT y WT
  //   BANK0
  //   BANK1
  //   BANK2
  //   BANK3
endmodule

module S_MIPS (
  input  Kbd_Available,
  input  [6:0] Kbd_ASCII_Data,
  input  [31:0] RAM_Out_0,
  input  [31:0] RAM_Out_1,
  input  Reset,
  input  [31:0] RAM_Out_2,
  input  Clock,
  input  [31:0] RAM_Out_3,
  input  [3:0] Read_Time,
  input  [3:0] Write_Time,
  output Kbd_Enable,
  output [15:0] Address,
  output Kbd_Clear,
  output TTY_Enable,
  output [6:0] TTY_ASCII_Data,
  output Stop,
  output [31:0] RAM_In_0,
  output [31:0] RAM_In_1,
  output [31:0] RAM_In_2,
  output [31:0] RAM_In_3,
  output [3:0] Mask,
  output nRead_Write,
  output Chip_Select
);


  // Other names for the same wires on the sheet: CLK = Clock; CLR = Reset; CS = Chip_Select;
  //   KBD_AVAIL = Kbd_Available; KBD_CLR = Kbd_Clear; KBD_DATA[6:0] = Kbd_ASCII_Data; RAM_A[15:0] = Address;
  //   RAM_INPUT_0[31:0] = RAM_In_0; RAM_INPUT_1[31:0] = RAM_In_1; RAM_INPUT_2[31:0] = RAM_In_2;
  //   RAM_INPUT_3[31:0] = RAM_In_3; RAM_MASK[3:0] = Mask; RAM_OUTPUT_0[31:0] = RAM_Out_0;
  //   RAM_OUTPUT_1[31:0] = RAM_Out_1; RAM_OUTPUT_2[31:0] = RAM_Out_2; RAM_OUTPUT_3[31:0] = RAM_Out_3;
  //   RW = nRead_Write; TTY_DATA[6:0] = TTY_ASCII_Data

  // Notes on the sheet:
  //   RAM ADDRESS
  //   DATA FROM RAM
  //   DATA TO RAM
  //   DATA WRITE MASK
  //   RAM TIMING
  //   RAM CONTROL
  //   KEYBOARD
  //   TTY
  //   SEQUENCING
endmodule

module RAM_Dispatcher (
  input  [3:0] WriteTime,
  input  Clock,
  input  CLR,
  output [31:0] Data,
  output [15:0] Address,
  output [3:0] Mask,
  output Finished,
  output Write
);

  wire demultiplexer_2_out1, demultiplexer_3_out1, End, IDLE_q, IncAddr, Load, or_1_out, or_2_out, While_q,
       WriteEnd;
  wire [3:0] counter_1_q;
  wire [31:0] CurrentAddress_q;

  Counter #(.width(32), .max('hffffffff)) CurrentAddress (
    .count(IncAddr), .Q({CurrentAddress_q[31:18], Address, CurrentAddress_q[1:0]}), .clk(Clock), .clr(CLR));  // open: load, D, carry
  or or_1 (or_1_out, IncAddr, demultiplexer_3_out1, Finished);
  D_Flip_Flop IDLE (.clk(Clock), .D(or_1_out), .Q(IDLE_q), .preset(CLR));  // open: Qn, en, reset
  Demultiplexer #(.enable("false")) demultiplexer_1 (.out0(Load), .out1(Finished), .in(IDLE_q), .sel(End));
  D_Flip_Flop While (.clk(Clock), .D(or_2_out), .Q(While_q), .reset(CLR));  // open: Qn, preset, en
  or or_2 (or_2_out, Write, Load);
  RAM_part #(.addrWidth(18), .dataWidth(32)) ram_1 (
    .addr({Address, CurrentAddress_q[1:0]}), .data(Data), .clk(Clock));  // open: sel, ld, clr
  Demultiplexer #(.enable("false")) demultiplexer_2 (
    .out0(Write), .out1(demultiplexer_2_out1), .in(While_q), .sel(WriteEnd));
  Decoder #(.select(2)) decoder_1 (
    .out0(Mask[0]), .out1(Mask[1]), .out2(Mask[2]), .out3(Mask[3]), .sel(CurrentAddress_q[1:0]));  // open: en
  Demultiplexer #(.enable("false")) demultiplexer_3 (
    .out0(IncAddr), .out1(demultiplexer_3_out1), .in(demultiplexer_2_out1), .sel(End));
  Counter #(.width(4), .max('hf)) counter_1 (
    .load(Load), .D(WriteTime), .count(Write), .Q(counter_1_q), .clk(Clock));  // open: carry, clr
  Comparator #(.width(32)) comparator_1 (.a(Data), .b({32{1'b1}}), .eq(End));  // open: gt, lt
  Comparator #(.width(4)) comparator_2 (.a(4'b0000), .b(counter_1_q), .eq(WriteEnd));  // open: gt, lt

  // Other names for the same wires on the sheet: CLK = Clock; Count = Write; WT[3:0] = WriteTime
endmodule

module Branch_Control_Unit (
  input  [31:0] in_1
);

  wire add, \and , div, divu, I, IE, J, mult, mulu, nop, \nor , \or , P, R, slt, sltu, sub, \xor ;

  Comparator #(.width(6)) comparator_1 (.a(in_1[5:0]), .b({6{1'b0}}), .eq(R));  // open: gt, lt
  Comparator #(.width(6)) comparator_2 (.a(in_1[5:0]), .b(6'b001000), .eq(J));  // open: gt, lt
  Comparator #(.width(6)) comparator_3 (.a(in_1[5:0]), .b(6'b011000), .eq(P));  // open: gt, lt
  Comparator #(.width(6)) comparator_4 (.a(in_1[5:0]), .b(6'b000111), .eq(IE));  // open: gt, lt
  nor nor_1 (I, R, J, P, IE);
  Comparator #(.width(6)) comparator_5 (.a(in_1[31:26]), .b({6{1'b0}}), .eq(nop));  // open: gt, lt
  Comparator #(.width(6)) comparator_6 (.a(in_1[31:26]), .b(6'b100000), .eq(add));  // open: gt, lt
  Comparator #(.width(6)) comparator_7 (.a(in_1[31:26]), .b(6'b101010), .eq(sub));  // open: gt, lt
  Comparator #(.width(6)) comparator_8 (.a(in_1[31:26]), .b({6{1'b0}}), .eq(mult));  // open: gt, lt
  Comparator #(.width(6)) comparator_9 (.a(in_1[31:26]), .b(6'b000001), .eq(mulu));  // open: gt, lt
  Comparator #(.width(6)) comparator_10 (.a(in_1[31:26]), .b(6'b001000), .eq(div));  // open: gt, lt
  Comparator #(.width(6)) comparator_11 (.a(in_1[31:26]), .b(6'b001001), .eq(divu));  // open: gt, lt
  Comparator #(.width(6)) comparator_12 (.a(in_1[31:26]), .b(6'b010010), .eq(slt));  // open: gt, lt
  Comparator #(.width(6)) comparator_13 (.a(in_1[31:26]), .b(6'b001000), .eq(\xor ));  // open: gt, lt
  Comparator #(.width(6)) comparator_14 (.a(in_1[31:26]), .b(6'b010011), .eq(sltu));  // open: gt, lt
  Comparator #(.width(6)) comparator_15 (.a(in_1[31:26]), .b(6'b000100), .eq(\and ));  // open: gt, lt
  Comparator #(.width(6)) comparator_16 (.a(in_1[31:26]), .b(6'b000101), .eq(\or ));  // open: gt, lt
  Comparator #(.width(6)) comparator_17 (.a(in_1[31:26]), .b(6'b001111), .eq(\nor ));  // open: gt, lt

  // Other names for the same wires on the sheet: _6_fisrt_input_bits[5:0] = in_1[5:0]; Input[31:0] = in_1;
  //   _6_last_bists_input[5:0] = in_1[31:26]
endmodule

module Instruction_Decoder (
  input  [31:0] in_1,
  output [5:0] Op_Code,
  output [4:0] Rt,
  output [15:0] Constante,
  output [5:0] Func_Code,
  output [4:0] Rd,
  output [4:0] Rs,
  output [4:0] x,
  output [25:0] Destino_salto
);


  assign Constante = in_1[31:16];
  assign Destino_salto = in_1[31:6];
  assign Func_Code = in_1[31:26];
  assign Op_Code = in_1[5:0];
  assign Rd = in_1[20:16];
  assign Rs = in_1[10:6];
  assign Rt = in_1[15:11];
  assign x = in_1[20:16];

  // Other names for the same wires on the sheet: Input[31:0] = in_1

  // Notes on the sheet:
  //   Instruction Decoder
endmodule

module ALU (
  input  [4:0] in_1,
  input  [4:0] in_2,
  output [9:0] result
);

  wire [4:0] add, div, mul, sub;

  Demultiplexer #(.select(4)) demultiplexer_1 (.in(result[0]));  // open: out0, out1, out2, out3, out4, out5, out6, out7, out8, out9, out10, out11, out12, out13, out14, out15, sel, en
  Adder #(.width(5)) adder_1 (.a(in_1), .b(in_2), .out(add));  // open: cin, cout
  Subtractor #(.width(5)) subtractor_1 (.a(in_1), .b(in_2), .out(sub));  // open: bin, bout
  Multiplier #(.width(5)) multiplier_1 (.a(in_1), .b(in_2), .out(mul));  // open: cin, cout
  Divider #(.width(5)) divider_1 (.a(in_1), .b(in_2), .out(div));  // open: upper, rem
  // Pins of 1 and 10 bits meet at result

  // Other names for the same wires on the sheet: a[4:0] = in_1; b[4:0] = in_2
endmodule

module Intrucciones__I (
  input  [31:0] Rs,
  input  [15:0] cons,
  input  [31:0] Rs_2,
  input  [15:0] cons_2,
  input  [31:0] Rs_3,
  input  [15:0] cons_3,
  input  [31:0] Rs_4,
  input  [15:0] in_8,
  input  [31:0] Rs_5,
  input  [15:0] in_10,
  output [31:0] Output,
  output [31:0] Output_2,
  output [31:0] Output_3
);

  wire [31:0] adder_2_out, adder_3_out;

  Adder #(.width(32)) adder_1 (.a(Rs), .b({{17{cons[15]}}, cons[14:0]}), .out(Output));  // open: cin, cout
  Comparator #(.width(32)) comparator_1 (
    .a(Rs_2), .b({{17{cons_2[15]}}, cons_2[14:0]}), .lt(Output_2[0]));  // open: gt, eq
  assign Output_3 = Rs_3 & {{16{1'b0}}, cons_3};  // AND_Gate and_1, 32 bits wide
  Adder #(.width(32)) adder_2 (.a(Rs_4), .b({{17{in_8[15]}}, in_8[14:0]}), .out(adder_2_out));  // open: cin, cout
  Adder #(.width(32)) adder_3 (.a(Rs_5), .b({{17{in_10[15]}}, in_10[14:0]}), .out(adder_3_out));  // open: cin, cout

  assign Output_2[31:1] = {31{1'b0}};

  // Other names for the same wires on the sheet: a = Output_2[0]

  // Notes on the sheet:
  //   addi
  //   slti
  //   andi
  //   lw
  //   sw
endmodule

module Instrucciones__R (
  input  [15:0] Rt,
  input  [15:0] Rs,
  input  [15:0] Rt_2,
  input  [15:0] Rs_2,
  output [31:0] Output,
  output [31:0] Output_2
);

  wire [15:0] complemento_a_2_simple_1_output, complemento_a_2_simple_2_output;

  Comparator #(.width(16)) comparator_1 (.a(Rt), .b(Rs), .gt(Output[0]));  // open: eq, lt
  complemento_a_2_simple complemento_a_2_simple_1 (.in_1(Rt_2), .Output(complemento_a_2_simple_1_output));
  complemento_a_2_simple complemento_a_2_simple_2 (.in_1(Rs_2), .Output(complemento_a_2_simple_2_output));
  Comparator #(.width(16)) comparator_2 (
    .a(complemento_a_2_simple_1_output), .b(complemento_a_2_simple_2_output), .gt(Output[0]));  // open: eq, lt

  assign Output[31:1] = {31{1'b0}};
  assign Output_2 = {{31{1'b0}}, Output[0]};

  // Other names for the same wires on the sheet: a = Output[0]

  // Notes on the sheet:
  //   slt
  //   sltu
endmodule

module complemento_a_2_simple (
  input  [15:0] in_1,
  output [15:0] Output
);

  wire [15:0] not_1_out;

  not not_1 (not_1_out[0], in_1[0]);
  not not_2 (not_1_out[1], in_1[1]);
  not not_3 (not_1_out[2], in_1[2]);
  not not_4 (not_1_out[3], in_1[3]);
  not not_5 (not_1_out[4], in_1[4]);
  not not_6 (not_1_out[5], in_1[5]);
  not not_7 (not_1_out[6], in_1[6]);
  not not_8 (not_1_out[7], in_1[7]);
  not not_9 (not_1_out[8], in_1[8]);
  not not_10 (not_1_out[9], in_1[9]);
  not not_11 (not_1_out[10], in_1[10]);
  not not_12 (not_1_out[11], in_1[11]);
  not not_13 (not_1_out[12], in_1[12]);
  not not_14 (not_1_out[13], in_1[13]);
  not not_15 (not_1_out[14], in_1[14]);
  not not_16 (not_1_out[15], in_1[15]);
  Adder #(.width(16)) adder_1 (.a(not_1_out), .b(16'h1), .out(Output));  // open: cin, cout
endmodule
